# Fritzing sketch sketch_dht11_display (saved by Fritzing 0.7.11b)
breadboards: 1

parts:
  U1 = Arduino Mega
  Arduino_Ethernet_Shield1 = Arduino Ethernet Shield  # not connected
  R1 = Rotary Potentiometer (Small) [maximum_resistance=100kΩ]
  LCD1 = LCD screen

nets:
  +5V: U1.+5V, R1.leg2, LCD1.VDD, LCD1.LED+
  N1: U1.D40, LCD1.DB6
  N2: U1.D41, LCD1.DB7
  N3: U1.D42, LCD1.RS
  N4: U1.D43, LCD1.E
  N5: U1.D44, LCD1.DB4
  N6: U1.D45, LCD1.DB5
  GND: U1.GND, R1.leg1, LCD1.VSS, LCD1.R/W, LCD1.LED-
  N7: R1.wiper, LCD1.V0
